# Fritzing sketch halloween-project (saved by Fritzing 0.9.3b)
circuit board: 13.1686cm x 7.58836cm
breadboards: 1

parts:
  PIR_Sensor = HC-SR501 Body Sensor Module
  YwRobot_Power_Supply1 = YwRobot Breadboard Power Supply [part_number=545043]
  WeMos_D1_Mini1 = WeMos D1 Mini
  Speaker = SPEAKER [package=pcb_mount_speaker]
  DFRobot_DFPlayer = DFRobot DFPlayer Mini [part_number=DFR0299]
  J2 = Basic Servo  # not connected
  J3 = Basic Servo  # not connected
  J4 = Basic Servo  # not connected
  J5 = Basic Servo  # not connected
  J6 = Basic Servo  # not connected
  J7 = Basic Servo  # not connected
  J8 = Basic Servo  # not connected
  J9 = Basic Servo  # not connected
  J1 = Basic Servo
  PCA9685 = Adafruit PCA9685 PWM/Servo Breakout [part_number=815]

nets:
  5V: PIR_Sensor.VCC, YwRobot_Power_Supply1.VCC, WeMos_D1_Mini1.5V, DFRobot_DFPlayer.VCC, J1.vcc, PCA9685.5.0V, PCA9685.PWRIN, PCA9685.VCC
  N1: PIR_Sensor.OUT, WeMos_D1_Mini1.D7
  GND: PIR_Sensor.GND, YwRobot_Power_Supply1.GND, WeMos_D1_Mini1.G, DFRobot_DFPlayer.GND-1, DFRobot_DFPlayer.GND-2, J1.gnd, PCA9685.GND
  N2: WeMos_D1_Mini1.D1, PCA9685.SCL
  N3: WeMos_D1_Mini1.D2, PCA9685.SDA
  N4: WeMos_D1_Mini1.D5, DFRobot_DFPlayer.TX
  N5: WeMos_D1_Mini1.D6, DFRobot_DFPlayer.RX
  N6: Speaker.+, DFRobot_DFPlayer.SPK_2
  N7: Speaker.-, DFRobot_DFPlayer.SPK_1
  N8: J1.pulse, PCA9685.PWM0

notes:
  5V
  servos 1-9 connected the same way in the next pins

custom parts:
  HC-SR501 Body Sensor Module: Pyroelectric Infrared PIR Motion Sensor Detector Module
  YwRobot Breadboard Power Supply: The YwRobot Breadboard Power Supply (MB-V2) has two power rails; they can be 5V or 3V3. Power to the module can be provided through the female USB socket or through the A10 (female) 2.1mm power jack.
  Adafruit PCA9685 PWM/Servo Breakout: Using only two pins, control 16 free-running PWM outputs! I2C-controlled PWM driver with a built in clock. Unlike the TLC5940 family, you do not need to continuously send it signal tying up your microcontroller, its completely free running! 5V compliant, which means you can control it from a 3.3V microcontroller and still safely drive up to 6V outputs (this is good for when you want to control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
